// Logisim project Vrata_Version0.0.1.circ as structural Verilog: 2 circuits, main circuit main
module main (
  output \Levá_zavírání ,
  output \Pravá_zavírání ,
  output \Zavřít_vrata ,
  output \Levá_otevřeno_zavřeno ,
  output \Pravá_otevřeno_zavřeno ,
  output ZAPNUTO_VYPNUTO
);

  wire and_2_out, and_3_out, and_4_out, and_5_out, button_1_out, clock_1_out;

  Clock clock_1 (.out(clock_1_out));
  buttonswitch buttonswitch_1 (.in_2(button_1_out), .out_3(ZAPNUTO_VYPNUTO), .in_1(and_4_out));
  Button button_1 (.out(button_1_out));
  and and_1 (\Levá_zavírání , \Pravá_zavírání , \Pravá_otevřeno_zavřeno );
  and and_2 (and_2_out, ZAPNUTO_VYPNUTO, clock_1_out);
  Counter #(.width(3), .max('h7), .ongoal("stay")) counter_1 (
    .load(\Levá_zavírání ), .carry(\Levá_otevřeno_zavřeno ), .clk(and_2_out));  // open: D, count, Q, clr
  and and_3 (and_3_out, \Levá_otevřeno_zavřeno , ZAPNUTO_VYPNUTO, clock_1_out);
  Counter #(.width(3), .max('h7), .ongoal("stay")) counter_2 (
    .load(\Pravá_zavírání ), .carry(\Pravá_otevřeno_zavřeno ), .clk(and_3_out));  // open: D, count, Q, clr
  and and_4 (and_4_out, \Levá_otevřeno_zavřeno , \Pravá_zavírání );
  and and_5 (and_5_out, \Pravá_otevřeno_zavřeno , ZAPNUTO_VYPNUTO, clock_1_out);
  Counter #(.width(3), .max('h7), .ongoal("stay")) counter_3 (
    .carry(\Pravá_zavírání ), .clk(and_5_out), .clr(and_4_out));  // open: load, D, count, Q

  assign \Zavřít_vrata  = \Pravá_zavírání ;

  // Notes on the sheet:
  //   START/STOP
endmodule

module buttonswitch (
  input  in_1,
  input  in_2,
  output out_3
);

  wire d_ff_1_qn, d_ff_2_q, or_1_out;

  or or_1 (or_1_out, in_2, in_1);
  D_Flip_Flop #(.trigger("high")) d_ff_1 (
    .clk(or_1_out), .D(d_ff_2_q), .Q(out_3), .Qn(d_ff_1_qn));  // open: preset, en, reset
  D_Flip_Flop d_ff_2 (.clk(or_1_out), .D(d_ff_1_qn), .Q(d_ff_2_q));  // open: Qn, preset, en, reset
endmodule
